# Fritzing sketch picow-proj-schematic (saved by Fritzing 1.0.0rc)
breadboards: 1

parts:
  LED1 = LED - 5mm [color="Red (633nm)" current=0.030A package="5 mm [THT]"]
  LED2 = LED - 5mm [color="Red (633nm)" current=0.030A package="5 mm [THT]"]
  R1 = Resistor [tolerance=±5% resistance=100 package="0805 [SMD]"]
  R2 = Resistor [tolerance=±5% resistance=100 package="0805 [SMD]"]
  S1 = Pushbutton [package="[THT]"]
  Mod1 = Raspberry Pi Pico W
  S2 = Pushbutton [package="[THT]"]

nets:
  N1: LED1.cathode, R2.Pin_0
  N2: LED1.anode, Mod1.pin_20
  N3: LED2.cathode, R1.Pin_0
  N4: LED2.anode, Mod1.pin_19
  N5: R1.Pin_1, R2.Pin_1, S1.Pin_1, S1.Pin_2, Mod1.pin_3, Mod1.pin_8, Mod1.pin_13, Mod1.pin_18, Mod1.pin_23, Mod1.pin_28, Mod1.pin_33, Mod1.pin_38, S2.Pin_1, S2.Pin_2
  N6: S1.Pin_3, S1.Pin_4, Mod1.pin_17
  N7: Mod1.pin_30, S2.Pin_3, S2.Pin_4

custom parts:
  Raspberry Pi Pico W: Raspberry Pi Pico W. Based around the RP2040 microcontroller the Pico W is a low cost microcontroller device bringing Raspberry Pi quality, cost, and easy of use to the microcontroller space. The areas marked KEEPOUT in pcb silkscreen should not have traces running through them to avoid shorts on a soldered in module!
